// Logisim project Lab1 tn2.circ as structural Verilog
module TN2 (
  input  x,
  input  y,
  input  z,
  output EQ1,
  output EQ2,
  output EQ3,
  output EQ4,
  output EQ5
);

  wire and_1_out, and_2_out, and_3_out, and_4_out, and_5_out, not_1_out, not_2_out, not_3_out, not_4_out,
       or_1_out, or_2_out, or_3_out, or_4_out, or_5_out;

  or or_1 (or_1_out, x, y);
  not not_1 (not_1_out, x);
  not not_2 (not_2_out, y);
  and and_1 (and_1_out, not_1_out, not_2_out);
  and and_2 (and_2_out, x, y);
  and and_3 (and_3_out, y, z);
  or or_2 (or_2_out, x, z);
  and and_4 (and_4_out, not_1_out, y);
  or or_3 (or_3_out, and_4_out, x);
  or or_4 (or_4_out, x, y);
  not not_3 (not_3_out, or_1_out);
  not not_4 (not_4_out, and_2_out);
  or or_5 (or_5_out, and_3_out, x);
  and and_5 (and_5_out, or_1_out, or_2_out);
  xnor xnor_1 (EQ1, not_3_out, and_1_out);
  xnor xnor_2 (EQ2, and_1_out, not_4_out);
  xnor xnor_3 (EQ3, or_5_out, and_5_out);
  xnor xnor_4 (EQ4, x, or_3_out);
  xnor xnor_5 (EQ5, or_3_out, or_4_out);
endmodule

module TN3 (
  input  A,
  input  B,
  input  A_2,
  input  C,
  input  B_2,
  input  C_2,
  input  D,
  input  D_2,
  output F_can,
  output F,
  output F_soP
);

  wire and_1_out, and_2_out, and_5_out, and_6_out, and_7_out, and_8_out, and_9_out, and_10_out, and_11_out,
       and_12_out, and_13_out, and_14_out, and_15_out, and_16_out, and_17_out, not_1_out, not_3_out,
       not_4_out, not_5_out, not_6_out;

  not not_1 (not_1_out, D_2);
  not not_2 (B_2, A_2);
  not not_3 (not_3_out, B_2);
  not not_4 (not_4_out, C_2);
  and and_1 (and_1_out, B_2, not_3_out, C_2, not_1_out);
  and and_2 (and_2_out, B_2, not_3_out, C_2, D_2);
  and and_3 (and_1_out, B_2, B_2, not_4_out, D_2);
  and and_4 (D, B_2, B_2, C_2, D_2);
  and and_5 (and_5_out, A_2, not_3_out, C_2, D_2);
  and and_6 (and_6_out, A_2, B_2, not_4_out, D_2);
  not not_5 (not_5_out, A);
  not not_6 (not_6_out, B);
  not not_7 (and_1_out, B_2);
  not not_8 (and_1_out, D);
  or or_1 (F, and_1_out, and_2_out, and_1_out, D, and_5_out, and_6_out);
  and and_7 (and_7_out, not_5_out, not_6_out, B_2, and_1_out);
  and and_8 (and_8_out, not_5_out, not_6_out, B_2, D);
  and and_9 (and_9_out, not_5_out, B, and_1_out, D);
  and and_10 (and_10_out, not_5_out, B, B_2, D);
  and and_11 (and_11_out, A, not_6_out, B_2, D);
  and and_12 (and_12_out, A, B, and_1_out, D);
  and and_13 (and_13_out, not_5_out, not_6_out, B_2);
  and and_14 (and_14_out, not_6_out, B_2, D);
  and and_15 (and_15_out, not_5_out, B, D);
  and and_16 (and_16_out, B, and_1_out, D);
  and and_17 (and_17_out, A, not_6_out, B_2, D);
  or or_2 (F_can, and_7_out, and_8_out, and_9_out, and_10_out, and_11_out, and_12_out);
  or or_3 (F_soP, and_13_out, and_14_out, and_15_out, and_16_out, and_17_out);

  assign C = B_2;
endmodule

module TN41 (
  input  A,
  input  B,
  input  C,
  input  D,
  output Fcan,
  output EQ1,
  output EQ2,
  output Fsop,
  output Fpos
);

  wire and_1_out, and_2_out, and_3_out, and_4_out, and_5_out, and_6_out, and_7_out, and_8_out, and_9_out,
       and_10_out, and_11_out, not_1_out, not_2_out, not_3_out, not_4_out, or_1_out, or_2_out, or_3_out,
       or_4_out, or_5_out;

  not not_1 (not_1_out, A);
  not not_2 (not_2_out, B);
  not not_3 (not_3_out, C);
  not not_4 (not_4_out, D);
  and and_1 (and_1_out, not_1_out, not_2_out, C, not_4_out);
  and and_2 (and_2_out, not_1_out, not_2_out, C, D);
  and and_3 (and_3_out, not_1_out, B, not_3_out, D);
  and and_4 (and_4_out, not_1_out, B, C, D);
  and and_5 (and_5_out, A, not_2_out, C, D);
  and and_6 (and_6_out, A, B, not_3_out, D);
  and and_7 (and_7_out, not_1_out, not_2_out, C);
  and and_8 (and_8_out, not_2_out, C, D);
  and and_9 (and_9_out, not_1_out, B, D);
  and and_10 (and_10_out, B, not_3_out, D);
  and and_11 (and_11_out, A, not_2_out, C, D);
  or or_1 (or_1_out, C, D);
  or or_2 (or_2_out, B, C);
  or or_3 (or_3_out, not_2_out, not_3_out, D);
  or or_4 (or_4_out, not_1_out, not_3_out, D);
  or or_5 (or_5_out, not_1_out, not_2_out, not_3_out, not_4_out);
  or or_6 (Fcan, and_1_out, and_2_out, and_3_out, and_4_out, and_5_out, and_6_out);
  or or_7 (Fsop, and_7_out, and_8_out, and_9_out, and_10_out, and_11_out);
  and and_12 (Fpos, or_1_out, or_2_out, or_3_out, or_4_out, or_5_out);
  xnor xnor_1 (EQ1, Fcan, Fsop);
  xnor xnor_2 (EQ2, Fcan, Fpos);
endmodule

module TN5 (
  input  A,
  input  B,
  input  C,
  output F
);

  wire xor_1_out;

  xor xor_1 (xor_1_out, A, B);
  xor xor_2 (F, xor_1_out, C);
endmodule
